// Logisim project Alu_mips.circ as structural Verilog: 1 circuit, main circuit main
module main (
  input  [3:0] x,
  input  [3:0] y,
  input  [2:0] Selection_bits,
  output [3:0] Output
);

  wire [3:0] adder_1_out, and_1_out, nor_1_out, or_1_out, subtractor_1_out;
  wire [15:0] shifter_1_out, shifter_2_out;

  assign and_1_out = y & x;  // AND_Gate and_1, 4 bits wide
  assign or_1_out = x | y;  // OR_Gate or_1, 4 bits wide
  Adder #(.width(4)) adder_1 (.a(x), .b(y), .out(adder_1_out));  // open: cin, cout
  Subtractor #(.width(4)) subtractor_1 (.a(x), .b(y), .out(subtractor_1_out));  // open: bin, bout
  assign nor_1_out = ~(x | y);  // NOR_Gate nor_1, 4 bits wide
  Shifter #(.width(16)) shifter_1 (.in({{12{1'b0}}, x}), .\dist (y), .out(shifter_1_out));
  Shifter #(.width(16), .shift("lr")) shifter_2 (.in({{12{1'b0}}, x}), .\dist (y), .out(shifter_2_out));
  Multiplexer #(.select(3), .width(4)) multiplexer_1 (
    .in0(and_1_out), .in1(or_1_out), .in2(adder_1_out), .in3(subtractor_1_out), .in4(nor_1_out),
    .in5(shifter_1_out[3:0]), .in6(4'b0000), .in7(shifter_2_out[3:0]), .out(Output), .sel(Selection_bits),
    .en(1'b1));
endmodule
