// Logisim project mips.circ as structural Verilog: 9 circuits, main circuit main
module main (
  input  ClearAll,
  output [3:0] out_2,
  output [3:0] Opcode,
  output [3:0] out_4,
  output [3:0] out_5,
  output [7:0] PC,
  output [3:0] out_7,
  output [3:0] out_8,
  output [3:0] out_9,
  output [3:0] out_10,
  output [3:0] DataRead,
  output [3:0] WriteData,
  output [3:0] zero,
  output [3:0] t0,
  output [3:0] t1,
  output [3:0] t2,
  output [3:0] t3,
  output [3:0] t4,
  output [3:0] sp
);

  wire alu_1_zero, and_1_out, and_2_out, CLK_out, control_1_alusrc, control_1_beq, control_1_bneq,
       control_1_jump, control_1_memread, control_1_memtoreg, control_1_memwrite, control_1_regdst,
       control_1_regwrite, not_1_out, or_1_out;
  wire [2:0] control_1_alu_ctrl;
  wire [3:0] multiplexer_4_out;
  wire [7:0] adder_1_out, adder_2_out, insextractor_1_jumpaddr, multiplexer_2_out, multiplexer_3_out,
       signextender_1_imm_8_out, zeroextender_1_addr_8_out;
  wire [15:0] insmemory_1_instruction;

  Register register_1 (.D(multiplexer_3_out), .Q(PC), .clk(CLK_out), .clr(ClearAll));  // open: en
  Adder adder_1 (.a(PC), .b(8'h1), .out(adder_1_out), .cin(1'b0));  // open: cout
  InsMemory insmemory_1 (.Addr_Instr(PC), .Instruction(insmemory_1_instruction));
  Clock CLK (.out(CLK_out));
  InsExtractor insextractor_1 (
    .InsInput(insmemory_1_instruction), .JumpAddr(insextractor_1_jumpaddr), .Opcode(Opcode),
    .SrcRegister1(out_9), .SrcRegister2(out_8), .Destination_Imm(out_2));
  SignExtender signextender_1 (.Imm_4_in(out_2), .Imm_8_out(signextender_1_imm_8_out));
  Control control_1 (
    .in_1(Opcode), .ALU_Ctrl(control_1_alu_ctrl), .RegWrite(control_1_regwrite), .ALUSrc(control_1_alusrc),
    .MemWrite(control_1_memwrite), .MemtoReg(control_1_memtoreg), .MemRead(control_1_memread),
    .Bneq(control_1_bneq), .beq(control_1_beq), .Jump(control_1_jump), .RegDst(control_1_regdst));
  Adder adder_2 (.a(adder_1_out), .b(signextender_1_imm_8_out), .out(adder_2_out));  // open: cin, cout
  Multiplexer #(.width(4), .enable("false")) multiplexer_1 (
    .in0(out_8), .in1(out_2), .out(out_7), .sel(control_1_regdst));
  Multiplexer #(.width(8), .enable("false")) multiplexer_2 (
    .in0(adder_1_out), .in1(adder_2_out), .out(multiplexer_2_out), .sel(or_1_out));
  and and_1 (and_1_out, alu_1_zero, control_1_beq);
  or or_1 (or_1_out, and_1_out, and_2_out);
  and and_2 (and_2_out, not_1_out, control_1_bneq);
  not not_1 (not_1_out, alu_1_zero);
  RegisterFile registerfile_1 (
    .ReadRegister1(out_9), .ReadRegister1_2(out_8), .WriteRegister(out_7), .WriteData(WriteData),
    .RegWrite(control_1_regwrite), .CLK(CLK_out), .Clear(ClearAll), .zero(zero), .t0(t0), .t1(t1), .t2(t2),
    .t3(t3), .t4(t4), .sp(sp), .ReadData1(out_5), .ReadData2(out_10));
  Multiplexer #(.width(8), .enable("false")) multiplexer_3 (
    .in0(multiplexer_2_out), .in1(insextractor_1_jumpaddr), .out(multiplexer_3_out), .sel(control_1_jump));
  Multiplexer #(.width(4), .enable("false")) multiplexer_4 (
    .in0(out_10), .in1(out_2), .out(multiplexer_4_out), .sel(control_1_alusrc));
  ALU alu_1 (.x(out_5), .y(multiplexer_4_out), .AluCtrl(control_1_alu_ctrl), .Zero(alu_1_zero), .Output(out_4));
  ZeroExtender zeroextender_1 (.Addr_4_in(out_4), .Addr_8_out(zeroextender_1_addr_8_out));
  DataMemory datamemory_1 (
    .Address(zeroextender_1_addr_8_out), .WriteData(out_10), .MemWrite(control_1_memwrite), .CLK(CLK_out),
    .MemRead(control_1_memread), .Clear(ClearAll), .ReadData(DataRead));
  Multiplexer #(.width(4), .enable("false")) multiplexer_5 (
    .in0(out_4), .in1(DataRead), .out(WriteData), .sel(control_1_memtoreg));
endmodule

module ALU (
  input  [2:0] AluCtrl,
  input  [3:0] x,
  input  [3:0] y,
  output Zero,
  output [3:0] Output
);

  wire [3:0] adder_1_out, and_1_out, nor_1_out, or_1_out, subtractor_1_out;
  wire [15:0] shifter_1_out, shifter_2_out;

  assign and_1_out = y & x;  // AND_Gate and_1, 4 bits wide
  assign or_1_out = x | y;  // OR_Gate or_1, 4 bits wide
  Adder #(.width(4)) adder_1 (.a(x), .b(y), .out(adder_1_out));  // open: cin, cout
  Subtractor #(.width(4)) subtractor_1 (.a(x), .b(y), .out(subtractor_1_out));  // open: bin, bout
  assign nor_1_out = ~(x | y);  // NOR_Gate nor_1, 4 bits wide
  Shifter #(.width(16)) shifter_1 (.in({{12{1'b0}}, x}), .\dist (y), .out(shifter_1_out));
  Shifter #(.width(16), .shift("lr")) shifter_2 (.in({{12{1'b0}}, x}), .\dist (y), .out(shifter_2_out));
  Multiplexer #(.select(3), .width(4), .disabled(0), .enable("false")) multiplexer_1 (
    .in0(and_1_out), .in1(or_1_out), .in2(adder_1_out), .in3(subtractor_1_out), .in4(nor_1_out),
    .in5(shifter_1_out[3:0]), .in6(4'b0000), .in7(shifter_2_out[3:0]), .out(Output), .sel(AluCtrl));
  nor nor_2 (Zero, Output[0], Output[1], Output[2], Output[3]);
endmodule

module Control (
  input  [3:0] in_1,
  output [2:0] ALU_Ctrl,
  output RegWrite,
  output ALUSrc,
  output MemWrite,
  output MemtoReg,
  output MemRead,
  output Bneq,
  output beq,
  output Jump,
  output RegDst
);

  ROM #(.addrWidth(4), .dataWidth(12)) rom_1 (
    .addr(in_1), .data({RegDst, Jump, beq, Bneq, MemRead, MemtoReg, MemWrite, ALUSrc, RegWrite, ALU_Ctrl}));  // open: sel

  // Notes on the sheet:
  //   contents of rom_1 (hex, n*v repeats v):
  //   da 103 1b 203 400 1a 32 809 80a 808 19 80c 18 80b 1d 1f
endmodule

// InM
module InsMemory (
  input  [7:0] Addr_Instr,
  output [15:0] Instruction
);

  ROM #(.dataWidth(16)) rom_1 (.addr(Addr_Instr), .data(Instruction));  // open: sel

  // Notes on the sheet:
  //   contents of rom_1 (hex, n*v repeats v):
  //   5021 5033 8231 8134 8125 6323 e222 3121 41f0 d415 2441 f441 323 9241 7452 41c0 566f 6610 566f 6620
  //   a114 610 5661 c330 630 5661 b333 41f0 1131 41f0 4100
endmodule

// RegFile
module RegisterFile (
  input  RegWrite,
  input  [3:0] ReadRegister1,
  input  [3:0] ReadRegister1_2,
  input  [3:0] WriteRegister,
  input  [3:0] WriteData,
  input  CLK,
  input  Clear,
  output [3:0] ReadData1,
  output [3:0] ReadData2,
  output [3:0] zero,
  output [3:0] t0,
  output [3:0] t1,
  output [3:0] t2,
  output [3:0] t3,
  output [3:0] t4,
  output [3:0] sp
);

  wire and_1_out, and_2_out, and_3_out, and_4_out, and_5_out, and_6_out, and_7_out, decoder_1_out0,
       decoder_1_out1, decoder_1_out2, decoder_1_out3, decoder_1_out4, decoder_1_out5, decoder_1_out6,
       multiplexer_2_out, multiplexer_3_out;
  wire [3:0] multiplexer_1_out;

  Decoder #(.select(4), .enable("false")) decoder_1 (
    .out0(decoder_1_out0), .out1(decoder_1_out1), .out2(decoder_1_out2), .out3(decoder_1_out3),
    .out4(decoder_1_out4), .out5(decoder_1_out5), .out6(decoder_1_out6), .sel(WriteRegister));  // open: out7, out8, out9, out10, out11, out12, out13, out14, out15
  and and_1 (and_1_out, decoder_1_out0, 1'b0);
  and and_2 (and_2_out, decoder_1_out1, RegWrite);
  and and_3 (and_3_out, decoder_1_out2, RegWrite);
  and and_4 (and_4_out, decoder_1_out3, RegWrite);
  and and_5 (and_5_out, decoder_1_out4, RegWrite);
  and and_6 (and_6_out, decoder_1_out5, RegWrite);
  and and_7 (and_7_out, decoder_1_out6, RegWrite);
  Multiplexer #(.width(4), .enable("false")) multiplexer_1 (
    .in0(WriteData), .in1(4'b1111), .out(multiplexer_1_out), .sel(Clear));
  Multiplexer #(.enable("false")) multiplexer_2 (.in0(and_7_out), .in1(Clear), .out(multiplexer_2_out), .sel(Clear));
  Multiplexer #(.enable("false")) multiplexer_3 (.in0(CLK), .in1(Clear), .out(multiplexer_3_out), .sel(Clear));
  Register #(.width(4)) u_Zero (.D(WriteData), .en(and_1_out), .Q(zero), .clk(CLK), .clr(Clear));
  Register #(.width(4)) u_t0 (.D(WriteData), .en(and_2_out), .Q(t0), .clk(CLK), .clr(Clear));
  Register #(.width(4)) u_t1 (.D(WriteData), .en(and_3_out), .Q(t1), .clk(CLK), .clr(Clear));
  Register #(.width(4)) u_t2 (.D(WriteData), .en(and_4_out), .Q(t2), .clk(CLK), .clr(Clear));
  Register #(.width(4)) u_t3 (.D(WriteData), .en(and_5_out), .Q(t3), .clk(CLK), .clr(Clear));
  Register #(.width(4)) u_t4 (.D(WriteData), .en(and_6_out), .Q(t4), .clk(CLK), .clr(Clear));
  Register #(.width(4)) u_sp (
    .D(multiplexer_1_out), .en(multiplexer_2_out), .Q(sp), .clk(multiplexer_3_out));  // open: clr
  Multiplexer #(.select(4), .width(4), .enable("false")) multiplexer_4 (
    .in0(zero), .in1(t0), .in2(t1), .in3(t2), .in4(t3), .in5(t4), .in6(sp), .out(ReadData1),
    .sel(ReadRegister1));  // open: in7, in8, in9, in10, in11, in12, in13, in14, in15
  Multiplexer #(.select(4), .width(4), .enable("false")) multiplexer_5 (
    .in0(zero), .in1(t0), .in2(t1), .in3(t2), .in4(t3), .in5(t4), .in6(sp), .out(ReadData2),
    .sel(ReadRegister1_2));  // open: in7, in8, in9, in10, in11, in12, in13, in14, in15

  // Notes on the sheet:
  //   Write data selection
  //   Enable Selection
  //   CLK selection
endmodule

// DM
module DataMemory (
  input  MemWrite,
  input  [7:0] Address,
  input  [3:0] WriteData,
  input  MemRead,
  input  Clear,
  input  CLK,
  output [3:0] ReadData
);

  RAM #(.dataWidth(4), .bus("separate")) ram_1 (
    .addr(Address), .din(WriteData), .data(ReadData), .str(MemWrite), .clk(CLK), .ld(MemRead), .clr(Clear));  // open: sel
endmodule

// InsExt
module InsExtractor (
  input  [15:0] InsInput,
  output [7:0] JumpAddr,
  output [3:0] Opcode,
  output [3:0] SrcRegister1,
  output [3:0] SrcRegister2,
  output [3:0] Destination_Imm
);


  assign Destination_Imm = InsInput[3:0];
  assign JumpAddr = InsInput[11:4];
  assign Opcode = InsInput[15:12];
  assign SrcRegister1 = InsInput[11:8];
  assign SrcRegister2 = InsInput[7:4];
endmodule

// SiE
module SignExtender (
  input  [3:0] Imm_4_in,
  output [7:0] Imm_8_out
);


  assign Imm_8_out = {{5{Imm_4_in[3]}}, Imm_4_in[2:0]};
endmodule

// ZX
module ZeroExtender (
  input  [3:0] Addr_4_in,
  output [7:0] Addr_8_out
);


  assign Addr_8_out = {4'b0000, Addr_4_in};
endmodule
